# Fritzing sketch LesPotmeter (saved by Fritzing 0.9.3b)
breadboards: 1

parts:
  R1 = Trimmer Potentiometer [maximum_resistance=10kΩ package=THT]
  Part1 = Arduino Uno (Rev3)

nets:
  N1: R1.leg1, Part1.GND
  N2: R1.wiper, Part1.A0
  N3: R1.leg2, Part1.5V
