# Fritzing sketch analog_knapp_bb (saved by Fritzing 0.9.3b)
breadboards: 1

parts:
  R1 = Resistor [tolerance=±5% resistance=220 package=THT]
  LED1 = LED - 5mm [color="Red (633nm)" package="5 mm [THT]"]
  S3 = Momentary Switch [package=ksa_sealed_tac_switch]

nets:
  N1: R1.Pin_0, S3.3
  N2: LED1.anode, S3.1
