# Fritzing sketch styr_led_fra_knapp (saved by Fritzing 0.9.3b)
breadboards: 1

parts:
  R1 = Resistor [tolerance=±5% resistance=220 package=THT]
  S3 = Momentary Switch [package=ksa_sealed_tac_switch]
  LED1 = LED - 5mm [color="Red (633nm)" package="5 mm [THT]"]
  R2 = Resistor [tolerance=±5% resistance=10k package=THT]

nets:
  N1: R1.Pin_1, LED1.anode
  N2: S3.1, R2.Pin_1
  N3: LED1.cathode, R2.Pin_0
