# Fritzing sketch fasitkonstruksjon (saved by Fritzing 0.9.3b)
breadboards: 1

parts:
  Part1 = Arduino Uno (Rev3)
  R1 = Trimmer Potentiometer [maximum_resistance=10kΩ package=THT]
  J1 = Basic Servo

nets:
  N1: Part1.A0, R1.wiper
  N2: Part1.D9_PWM, J1.pulse
  5V: Part1.5V, R1.leg1, R1.leg2, J1.vcc
  GND: Part1.GND, J1.gnd
